// Logisim project ALU.circ as structural Verilog: 1 circuit, main circuit ALU
module ALU (
  input  [3:0] ALUOp,
  input  m,
  input  Cin,
  input  [15:0] Op0,
  input  [15:0] Op1,
  output A_eq_B,
  output [15:0] ALUOut
);

  wire sn74ls181_1_a_eq_b, sn74ls181_1_cout, sn74ls181_2_a_eq_b, sn74ls181_2_cout, sn74ls181_3_a_eq_b,
       sn74ls181_3_cout, sn74ls181_4_a_eq_b, sn74ls181_4_cout;

  sn74ls181 sn74ls181_1 (
    .A1(Op0[1]), .B3(Op1[3]), .A3(Op0[3]), .B2(Op1[2]), .A2(Op0[2]), .B1(Op1[1]), .B0(Op1[0]), .A0(Op0[0]),
    .M(m), .Cin(Cin), .s0(ALUOp[0]), .s1(ALUOp[1]), .s2(ALUOp[2]), .s3(ALUOp[3]), .F1(ALUOut[1]),
    .F0(ALUOut[0]), .Cout(sn74ls181_1_cout), .F3(ALUOut[3]), .F2(ALUOut[2]), .A_eq_B(sn74ls181_1_a_eq_b));  // open: notG_or_Y, notP_or_X
  sn74ls181 sn74ls181_2 (
    .A1(Op0[5]), .B3(Op1[7]), .A3(Op0[7]), .B2(Op1[6]), .A2(Op0[6]), .B1(Op1[5]), .B0(Op1[4]), .A0(Op0[4]),
    .M(m), .Cin(sn74ls181_1_cout), .s0(ALUOp[0]), .s1(ALUOp[1]), .s2(ALUOp[2]), .s3(ALUOp[3]),
    .F1(ALUOut[5]), .F0(ALUOut[4]), .Cout(sn74ls181_2_cout), .F3(ALUOut[7]), .F2(ALUOut[6]),
    .A_eq_B(sn74ls181_2_a_eq_b));  // open: notG_or_Y, notP_or_X
  sn74ls181 sn74ls181_3 (
    .A1(Op0[9]), .B3(Op1[11]), .A3(Op0[11]), .B2(Op1[10]), .A2(Op0[10]), .B1(Op1[9]), .B0(Op1[8]),
    .A0(Op0[8]), .M(m), .Cin(sn74ls181_2_cout), .s0(ALUOp[0]), .s1(ALUOp[1]), .s2(ALUOp[2]), .s3(ALUOp[3]),
    .F1(ALUOut[9]), .F0(ALUOut[8]), .Cout(sn74ls181_3_cout), .F3(ALUOut[11]), .F2(ALUOut[10]),
    .A_eq_B(sn74ls181_3_a_eq_b));  // open: notG_or_Y, notP_or_X
  sn74ls181 sn74ls181_4 (
    .A1(Op0[13]), .B3(Op1[15]), .A3(Op0[15]), .B2(Op1[14]), .A2(Op0[14]), .B1(Op1[13]), .B0(Op1[12]),
    .A0(Op0[12]), .M(m), .Cin(sn74ls181_3_cout), .s0(ALUOp[0]), .s1(ALUOp[1]), .s2(ALUOp[2]), .s3(ALUOp[3]),
    .F1(ALUOut[13]), .F0(ALUOut[12]), .Cout(sn74ls181_4_cout), .F3(ALUOut[15]), .F2(ALUOut[14]),
    .A_eq_B(sn74ls181_4_a_eq_b));  // open: notG_or_Y, notP_or_X
  and and_1 (A_eq_B, sn74ls181_1_a_eq_b, sn74ls181_2_a_eq_b, sn74ls181_3_a_eq_b, sn74ls181_4_a_eq_b);

  // Notes on the sheet:
  //   MSB di B
  //   MSB di A
  //   MSB del ris
  //   Cin
endmodule
