// Logisim project cpu_circuit.circ as structural Verilog: 2 circuits, main circuit main
module main (
  input  isInit
);

  wire alu_1_p3, and_1_out, clock_1_out, control_unit_1_p2, flags_1_p2, instruction_decoder_1_p2,
       instruction_decoder_1_p5, mask_checker_1_equal, or_1_out, undriven_2, undriven_3, undriven_4,
       undriven_7, undriven_8;
  wire [1:0] control_unit_1_p1, undriven_6;
  wire [2:0] flags_1_p1, instruction_decoder_1_p3;
  wire [3:0] instruction_decoder_1_p4, multiplexer_1_out;
  wire [3:3] flags_1_p1_2;
  wire [9:0] undriven_5;
  wire [15:0] bit_extender_1_out, bit_extender_2_out, bit_extender_3_out, instruction_ram_1_instruction,
       multiplexer_2_out, multiplexer_3_out, multiplexer_4_out, program_counter_1_instraddr,
       register_file_1_p2, undriven;

  program_counter program_counter_1 (
    .CLK(clock_1_out), .WE(clock_1_out), .isJumping(or_1_out), .AddrImm(multiplexer_2_out),
    .AddrReg(undriven), .InitValue({16{1'b0}}), .JumpSrc(undriven_2), .isInit(isInit),
    .InstrAddr(program_counter_1_instraddr));
  or or_1 (or_1_out, and_1_out, undriven_3);
  and and_1 (and_1_out, mask_checker_1_equal, undriven_4);
  instruction_RAM instruction_ram_1 (
    .InstrIN({16{1'b0}}), .InstrAddr(program_counter_1_instraddr), .WE(1'b0), .CLK(clock_1_out),
    .Instruction(instruction_ram_1_instruction));
  Clock clock_1 (.out(clock_1_out));
  mask_checker mask_checker_1 (.mask(instruction_decoder_1_p3), .flags(flags_1_p1), .equal(mask_checker_1_equal));
  // instruction_decoder instruction_decoder_1: pin names not known; wires that end beside it: instruction_ram_1_instruction, instruction_decoder_1_p2, instruction_decoder_1_p3, instruction_decoder_1_p4, instruction_decoder_1_p5
  Multiplexer #(.select(2), .width(4)) multiplexer_1 (
    .in0(instruction_decoder_1_p4), .in1(4'b0011), .in2(4'b0010), .out(multiplexer_1_out),
    .sel(control_unit_1_p1));  // open: in3
  assign bit_extender_1_out = {{6{undriven_5[9]}}, undriven_5};  // Bit_Extender bit_extender_1
  assign bit_extender_2_out = {{8{undriven_5[9]}}, undriven_5[9:2]};  // Bit_Extender bit_extender_2
  assign bit_extender_3_out = {{10{undriven_5[9]}}, undriven_5[9:4]};  // Bit_Extender bit_extender_3
  // flags flags_1: pin names not known; wires that end beside it: {flags_1_p1_2[3], flags_1_p1}, flags_1_p2
  Multiplexer #(.select(2), .width(16)) multiplexer_2 (
    .in0(bit_extender_1_out), .in1(bit_extender_2_out), .in2(bit_extender_3_out), .out(multiplexer_2_out),
    .sel(undriven_6));  // open: in3
  // control_unit control_unit_1: pin names not known; wires that end beside it: control_unit_1_p1[0], control_unit_1_p2
  // register_file register_file_1: pin names not known; wires that end beside it: multiplexer_1_out, register_file_1_p2
  Multiplexer #(.width(16)) multiplexer_3 (
    .in0(undriven), .in1(program_counter_1_instraddr), .out(multiplexer_3_out), .sel(undriven_7));
  Multiplexer #(.width(16)) multiplexer_4 (
    .in0(register_file_1_p2), .in1(multiplexer_2_out), .out(multiplexer_4_out), .sel(undriven_8));
  // ALU alu_1: pin names not known; wires that end beside it: multiplexer_4_out, control_unit_1_p2, alu_1_p3

  // Notes on the sheet:
  //   should WE = CLK for real?
  //   in this circuit there must not be input pins
  //   A Clock module should be better
  //   currently not using 4th flags bit
  //   rd
  //   ra=t3
  //   lui_rd=t2
  //   00 = rd
  //   01 = ra
  //   10 = lui_rd
  //   missing RF input "T/S"
  //   using the 74175 because there is no pre build 74173
  //   only difference is that this has an asynchronous reset
  //   the other on (74173) has enable pin, so and gate used
  //   in this circuit is not necessary
endmodule

module mask_checker (
  input  [2:0] mask,
  input  [2:0] flags,
  output equal
);

  Comparator #(.width(3)) comparator_1 (.a(mask), .b(flags), .eq(equal));  // open: gt, lt
endmodule
